// Logisim project Sayeem_CS.circ as structural Verilog: 13 circuits, main circuit main
module main (
  input  in_1,
  input  in_2,
  output [3:0] out_3,
  output [7:0] out_4,
  output [7:0] out_5,
  output [7:0] out_6,
  output [7:0] out_7,
  output [7:0] out_8,
  output [7:0] out_9,
  output [7:0] out_10,
  output [7:0] out_11,
  output [7:0] out_12,
  output [7:0] out_13,
  output [7:0] out_14,
  output [7:0] out_15,
  output [7:0] out_16,
  output [7:0] out_17,
  output [7:0] out_18,
  output [7:0] out_19,
  output [7:0] out_20,
  output [7:0] out_21,
  output [3:0] out_22,
  output [3:0] out_23,
  output [7:0] out_24,
  output [3:0] out_25,
  output [7:0] out_26,
  output [7:0] out_27
);

  wire a_in, a_out, alu_out, alu_sub, b_in, b_out, clk, ins_reg_in_en, ins_reg_out_en, mar_in_en, pc_en,
       pc_in_en, pc_out, ram_rd, rotate_in_en, rotate_out_en, shift_in_en, shift_out_en, sr_amount_in,
       sram_rd, sram_wr;
  wire [7:0] ram_1_dout;
  wire [7:4] reg_gp_1_reg_int_out;

  rotator rotator_1 (
    .data({out_24[7:4], out_22}), .rotate_out_en(rotate_out_en), .rotate_in_en(rotate_in_en), .clk(clk),
    .d_n_amount({out_24[7:4], out_22}), .rotate_amount_in(sr_amount_in),
    .rotate_data_out({out_24[7:4], out_22}));
  b_shifter b_shifter_1 (
    .data({out_24[7:4], out_22}), .shift_out_en(shift_out_en), .shift_in_en(shift_in_en), .clk(clk),
    .d_n_amount({out_24[7:4], out_22}), .shift_amount_in(sr_amount_in), .shift_data_out({out_24[7:4], out_22}));
  assign out_26 = in_1 ? {out_24[7:4], out_22} : 8'bz;  // Controlled_Buffer controlled_buffer_1
  pcWithLoader pcwithloader_1 (
    .pc_en(pc_en), .pc_in(out_22), .pc_in_en(pc_in_en), .pc_reset(in_2), .pc_clk(clk), .pc_out_en(pc_out),
    .pc_value(out_3), .pc_out(out_22));
  sram sram_1 (
    .sram_rd(sram_rd), .sram_wr(sram_wr), .sram_d_in({out_24[7:4], out_22}),
    .mar_d_in({out_24[7:4], out_22}), .mar_in_en(mar_in_en), .sram_clk(clk),
    .sram_d_out({out_24[7:4], out_22}), .out_8(out_5), .out_9(out_6), .out_10(out_7), .out_11(out_8),
    .out_12(out_9), .out_13(out_10), .out_14(out_12), .out_15(out_13), .out_16(out_14), .out_17(out_15),
    .out_18(out_16), .out_19(out_17), .out_20(out_18), .out_21(out_19), .out_22(out_20), .out_23(out_21));
  reg_gp reg_gp_1 (
    .reg_in(out_26), .reg_in_en(mar_in_en), .reg_clk(clk), .reg_int_out({reg_gp_1_reg_int_out, out_25}));  // open: reg_out_en, reg_out
  assign {out_24[7:4], out_22} = in_1 ? out_27 : 8'bz;  // Controlled_Buffer controlled_buffer_2
  RAM #(.addrWidth(4), .trigger("falling")) ram_1 (
    .addr(out_25), .oe(ram_rd), .clk(clk), .dout(ram_1_dout));  // open: we, din
  reg_gp reg_gp_2 (
    .reg_in({out_24[7:4], out_22}), .reg_in_en(a_in), .reg_clk(clk), .reg_out_en(a_out), .reg_int_out(out_4),
    .reg_out({out_24[7:4], out_22}));
  reg_gp reg_gp_3 (
    .reg_in({out_24[7:4], out_22}), .reg_in_en(b_in), .reg_clk(clk), .reg_out_en(b_out),
    .reg_int_out(out_11), .reg_out({out_24[7:4], out_22}));
  assign out_27 = ram_rd ? ram_1_dout : 8'bz;  // Controlled_Buffer controlled_buffer_3
  ins_reg ins_reg_1 (
    .ins_reg_in({out_24[7:4], out_22}), .ins_reg_in_en(ins_reg_in_en), .clk(clk),
    .ins_reg_out_en(ins_reg_out_en), .add_outs(out_22), .ins_out(out_23));
  alu alu_1 (
    .alu_in_1(out_4), .alu_out_en(alu_out), .alu_sub(alu_sub), .alu_in_2(out_11),
    .alu_out({out_24[7:4], out_22}));  // open: alu_carry_out
  cs cs_1 (
    .clk(clk), .ring_reset(in_2), .opcode_in(out_23), .debug(in_1), .ins_in_en(ins_reg_in_en), .b_in(b_in),
    .b_out(b_out), .sram_wr(sram_wr), .a_in(a_in), .alu_out(alu_out), .alu_sub(alu_sub),
    .shift_in_en(shift_in_en), .shift_out_en(shift_out_en), .rotate_in_en(rotate_in_en),
    .rotate_out_en(rotate_out_en), .a_out(a_out), .pc_in_en(pc_in_en), .ins_out_en(ins_reg_out_en),
    .sr_amount_in(sr_amount_in), .pc_out_en(pc_out), .ram_rd(ram_rd), .pc_en(pc_en), .mar_in(mar_in_en),
    .sram_rd(sram_rd));
  Clock clock_1 (.out(clk));

  assign out_24[3:0] = out_22;

  // Other names for the same wires on the sheet: debug = in_1; debug_data[7:0] = out_27;
  //   debug_data_out[7:0] = {out_24[7:4], out_22}; pc_reset = in_2

  // Notes on the sheet:
  //   RAM Data Input
  //   Clock and reset
endmodule

module reg_gp (
  input  [7:0] reg_in,
  input  reg_in_en,
  input  reg_clk,
  input  reg_out_en,
  output [7:0] reg_int_out,
  output [7:0] reg_out
);

  wire multiplexer_1_out, multiplexer_2_out, multiplexer_3_out, multiplexer_4_out, multiplexer_5_out,
       multiplexer_6_out, multiplexer_7_out, multiplexer_8_out;

  Multiplexer multiplexer_1 (.in0(reg_int_out[7]), .in1(reg_in[7]), .out(multiplexer_1_out), .sel(reg_in_en));
  D_Flip_Flop d_ff_1 (.D(multiplexer_1_out), .clk(reg_clk), .Q(reg_int_out[7]));  // open: Qn, preset, reset
  assign reg_out[7] = reg_out_en ? reg_int_out[7] : 1'bz;  // Controlled_Buffer controlled_buffer_1
  Multiplexer multiplexer_2 (.in0(reg_int_out[6]), .in1(reg_in[6]), .out(multiplexer_2_out), .sel(reg_in_en));
  D_Flip_Flop d_ff_2 (.D(multiplexer_2_out), .clk(reg_clk), .Q(reg_int_out[6]));  // open: Qn, preset, reset
  Multiplexer multiplexer_3 (.in0(reg_int_out[5]), .in1(reg_in[5]), .out(multiplexer_3_out), .sel(reg_in_en));
  assign reg_out[6] = reg_out_en ? reg_int_out[6] : 1'bz;  // Controlled_Buffer controlled_buffer_2
  D_Flip_Flop d_ff_3 (.D(multiplexer_3_out), .clk(reg_clk), .Q(reg_int_out[5]));  // open: Qn, preset, reset
  Multiplexer multiplexer_4 (.in0(reg_int_out[4]), .in1(reg_in[4]), .out(multiplexer_4_out), .sel(reg_in_en));
  assign reg_out[5] = reg_out_en ? reg_int_out[5] : 1'bz;  // Controlled_Buffer controlled_buffer_3
  D_Flip_Flop d_ff_4 (.D(multiplexer_4_out), .clk(reg_clk), .Q(reg_int_out[4]));  // open: Qn, preset, reset
  Multiplexer multiplexer_5 (.in0(reg_int_out[3]), .in1(reg_in[3]), .out(multiplexer_5_out), .sel(reg_in_en));
  assign reg_out[4] = reg_out_en ? reg_int_out[4] : 1'bz;  // Controlled_Buffer controlled_buffer_4
  D_Flip_Flop d_ff_5 (.D(multiplexer_5_out), .clk(reg_clk), .Q(reg_int_out[3]));  // open: Qn, preset, reset
  Multiplexer multiplexer_6 (.in0(reg_int_out[2]), .in1(reg_in[2]), .out(multiplexer_6_out), .sel(reg_in_en));
  D_Flip_Flop d_ff_6 (.D(multiplexer_6_out), .clk(reg_clk), .Q(reg_int_out[2]));  // open: Qn, preset, reset
  assign reg_out[3] = reg_out_en ? reg_int_out[3] : 1'bz;  // Controlled_Buffer controlled_buffer_5
  assign reg_out[2] = reg_out_en ? reg_int_out[2] : 1'bz;  // Controlled_Buffer controlled_buffer_6
  Multiplexer multiplexer_7 (.in0(reg_int_out[1]), .in1(reg_in[1]), .out(multiplexer_7_out), .sel(reg_in_en));
  D_Flip_Flop d_ff_7 (.D(multiplexer_7_out), .clk(reg_clk), .Q(reg_int_out[1]));  // open: Qn, preset, reset
  assign reg_out[1] = reg_out_en ? reg_int_out[1] : 1'bz;  // Controlled_Buffer controlled_buffer_7
  Multiplexer multiplexer_8 (.in0(reg_int_out[0]), .in1(reg_in[0]), .out(multiplexer_8_out), .sel(reg_in_en));
  D_Flip_Flop d_ff_8 (.D(multiplexer_8_out), .clk(reg_clk), .Q(reg_int_out[0]));  // open: Qn, preset, reset
  assign reg_out[0] = reg_out_en ? reg_int_out[0] : 1'bz;  // Controlled_Buffer controlled_buffer_8

  // Notes on the sheet:
  //   Input
  //   Input Control
  //   Clock
  //   Output Control
  //   Memory
  //   Internal Output
  //   Output
endmodule

module alu (
  input  [7:0] alu_in_1,
  input  alu_out_en,
  input  alu_sub,
  input  [7:0] alu_in_2,
  output alu_carry_out,
  output [7:0] alu_out
);

  wire adder_2_cout, adder_3_cout, adder_4_cout, adder_5_cout, adder_6_cout, adder_7_cout, adder_8_cout,
       xor_1_out, xor_2_out, xor_3_out, xor_4_out, xor_5_out, xor_6_out, xor_7_out, xor_8_out;
  wire [7:0] adder_8_out;

  Adder #(.width(1)) adder_1 (
    .a(alu_in_1[7]), .b(xor_1_out), .out(adder_8_out[7]), .cin(adder_2_cout), .cout(alu_carry_out));
  xor xor_1 (xor_1_out, alu_in_2[7], alu_sub);
  Adder #(.width(1)) adder_2 (
    .a(alu_in_1[6]), .b(xor_2_out), .out(adder_8_out[6]), .cin(adder_3_cout), .cout(adder_2_cout));
  xor xor_2 (xor_2_out, alu_in_2[6], alu_sub);
  Adder #(.width(1)) adder_3 (
    .a(alu_in_1[5]), .b(xor_3_out), .out(adder_8_out[5]), .cin(adder_4_cout), .cout(adder_3_cout));
  xor xor_3 (xor_3_out, alu_in_2[5], alu_sub);
  Adder #(.width(1)) adder_4 (
    .a(alu_in_1[4]), .b(xor_4_out), .out(adder_8_out[4]), .cin(adder_5_cout), .cout(adder_4_cout));
  xor xor_4 (xor_4_out, alu_in_2[4], alu_sub);
  Adder #(.width(1)) adder_5 (
    .a(alu_in_1[3]), .b(xor_5_out), .out(adder_8_out[3]), .cin(adder_6_cout), .cout(adder_5_cout));
  xor xor_5 (xor_5_out, alu_in_2[3], alu_sub);
  Adder #(.width(1)) adder_6 (
    .a(alu_in_1[2]), .b(xor_6_out), .out(adder_8_out[2]), .cin(adder_7_cout), .cout(adder_6_cout));
  xor xor_6 (xor_6_out, alu_in_2[2], alu_sub);
  Adder #(.width(1)) adder_7 (
    .a(alu_in_1[1]), .b(xor_7_out), .out(adder_8_out[1]), .cin(adder_8_cout), .cout(adder_7_cout));
  xor xor_7 (xor_7_out, alu_in_2[1], alu_sub);
  Adder #(.width(1)) adder_8 (.a(alu_in_1[0]), .b(xor_8_out), .out(adder_8_out[0]), .cin(alu_sub), .cout(adder_8_cout));
  xor xor_8 (xor_8_out, alu_in_2[0], alu_sub);
  assign alu_out = alu_out_en ? adder_8_out : 8'bz;  // Controlled_Buffer controlled_buffer_1

  // Notes on the sheet:
  //   Input 1
  //   Carry Output
  //   Subtract Control
  //   Full Adders
  //   Input 2
  //   Output Control
  //   ALU Output
endmodule

module pc (
  input  pc_en,
  input  pc_clk,
  input  pc_reset,
  input  pc_out_en,
  output [3:0] pc_value,
  output [3:0] pc_out
);

  wire j_k_ff_2_qn, j_k_ff_3_qn, j_k_ff_4_qn;

  J_K_Flip_Flop j_k_ff_1 (
    .J(pc_en), .K(pc_en), .clk(j_k_ff_2_qn), .Q(pc_value[3]), .reset(pc_reset));  // open: Qn, preset
  J_K_Flip_Flop j_k_ff_2 (
    .J(pc_en), .K(pc_en), .clk(j_k_ff_3_qn), .Q(pc_value[2]), .Qn(j_k_ff_2_qn), .reset(pc_reset));  // open: preset
  J_K_Flip_Flop j_k_ff_3 (
    .J(pc_en), .K(pc_en), .clk(j_k_ff_4_qn), .Q(pc_value[1]), .Qn(j_k_ff_3_qn), .reset(pc_reset));  // open: preset
  J_K_Flip_Flop j_k_ff_4 (
    .J(pc_en), .K(pc_en), .clk(pc_clk), .Q(pc_value[0]), .Qn(j_k_ff_4_qn), .reset(pc_reset));  // open: preset
  assign pc_out = pc_out_en ? pc_value : 4'bz;  // Controlled_Buffer controlled_buffer_1

  // Notes on the sheet:
  //   Clock
  //   Reset
  //   Output Control
  //   Count Control
  //   Counter Output
endmodule

module dec_4x16 (
  input  [3:0] dec_in,
  output [15:0] dec_out
);

  wire not_1_out, not_2_out, not_3_out, not_4_out;

  not not_1 (not_1_out, dec_in[3]);
  not not_2 (not_2_out, dec_in[2]);
  not not_3 (not_3_out, dec_in[1]);
  not not_4 (not_4_out, dec_in[0]);
  and and_1 (dec_out[0], not_4_out, not_3_out, not_2_out, not_1_out);
  and and_2 (dec_out[1], dec_in[0], not_3_out, not_2_out, not_1_out);
  and and_3 (dec_out[2], not_4_out, dec_in[1], not_2_out, not_1_out);
  and and_4 (dec_out[3], dec_in[0], dec_in[1], not_2_out, not_1_out);
  and and_5 (dec_out[4], not_4_out, not_3_out, dec_in[2], not_1_out);
  and and_6 (dec_out[5], dec_in[0], not_3_out, dec_in[2], not_1_out);
  and and_7 (dec_out[6], not_4_out, dec_in[1], dec_in[2], not_1_out);
  and and_8 (dec_out[7], dec_in[0], dec_in[1], dec_in[2], not_1_out);
  and and_9 (dec_out[8], not_4_out, not_3_out, not_2_out, dec_in[3]);
  and and_10 (dec_out[9], dec_in[0], not_3_out, not_2_out, dec_in[3]);
  and and_11 (dec_out[10], not_4_out, dec_in[1], not_2_out, dec_in[3]);
  and and_12 (dec_out[11], dec_in[0], dec_in[1], not_2_out, dec_in[3]);
  and and_13 (dec_out[12], not_4_out, not_3_out, dec_in[2], dec_in[3]);
  and and_14 (dec_out[13], dec_in[0], not_3_out, dec_in[2], dec_in[3]);
  and and_15 (dec_out[14], not_4_out, dec_in[1], dec_in[2], dec_in[3]);
  and and_16 (dec_out[15], dec_in[0], dec_in[1], dec_in[2], dec_in[3]);
endmodule

module sram_cell (
  input  [7:0] data_in,
  input  wr_en,
  input  clk,
  input  cs,
  input  rd_en,
  output [7:0] memory_content,
  output [7:0] data_out
);

  wire and_1_out, and_2_out;

  and and_1 (and_1_out, wr_en, cs);
  and and_2 (and_2_out, cs, rd_en);
  reg_gp reg_gp_1 (
    .reg_in(data_in), .reg_in_en(and_1_out), .reg_clk(clk), .reg_out_en(and_2_out),
    .reg_int_out(memory_content), .reg_out(data_out));
endmodule

module sram (
  input  sram_rd,
  input  sram_wr,
  input  [7:0] sram_d_in,
  input  [7:0] mar_d_in,
  input  mar_in_en,
  input  sram_clk,
  output [7:0] sram_d_out,
  output [7:0] out_8,
  output [7:0] out_9,
  output [7:0] out_10,
  output [7:0] out_11,
  output [7:0] out_12,
  output [7:0] out_13,
  output [7:0] out_14,
  output [7:0] out_15,
  output [7:0] out_16,
  output [7:0] out_17,
  output [7:0] out_18,
  output [7:0] out_19,
  output [7:0] out_20,
  output [7:0] out_21,
  output [7:0] out_22,
  output [7:0] out_23
);

  wire [7:0] controlled_buffer_1_out, reg_gp_1_reg_int_out;
  wire [15:0] dec_4x16_1_dec_out;

  reg_gp reg_gp_1 (
    .reg_in(mar_d_in), .reg_in_en(mar_in_en), .reg_clk(sram_clk), .reg_int_out(reg_gp_1_reg_int_out));  // open: reg_out_en, reg_out
  dec_4x16 dec_4x16_1 (.dec_in(reg_gp_1_reg_int_out[3:0]), .dec_out(dec_4x16_1_dec_out));
  assign controlled_buffer_1_out = sram_wr ? sram_d_in : 8'bz;  // Controlled_Buffer controlled_buffer_1
  sram_cell sram_cell_1 (
    .data_in(controlled_buffer_1_out), .wr_en(sram_wr), .clk(sram_clk), .cs(dec_4x16_1_dec_out[0]),
    .rd_en(sram_rd), .memory_content(out_8), .data_out(controlled_buffer_1_out));
  sram_cell sram_cell_2 (
    .data_in(controlled_buffer_1_out), .wr_en(sram_wr), .clk(sram_clk), .cs(dec_4x16_1_dec_out[1]),
    .rd_en(sram_rd), .memory_content(out_9), .data_out(controlled_buffer_1_out));
  sram_cell sram_cell_3 (
    .data_in(controlled_buffer_1_out), .wr_en(sram_wr), .clk(sram_clk), .cs(dec_4x16_1_dec_out[2]),
    .rd_en(sram_rd), .memory_content(out_10), .data_out(controlled_buffer_1_out));
  sram_cell sram_cell_4 (
    .data_in(controlled_buffer_1_out), .wr_en(sram_wr), .clk(sram_clk), .cs(dec_4x16_1_dec_out[3]),
    .rd_en(sram_rd), .memory_content(out_11), .data_out(controlled_buffer_1_out));
  sram_cell sram_cell_5 (
    .data_in(controlled_buffer_1_out), .wr_en(sram_wr), .clk(sram_clk), .cs(dec_4x16_1_dec_out[4]),
    .rd_en(sram_rd), .memory_content(out_12), .data_out(controlled_buffer_1_out));
  sram_cell sram_cell_6 (
    .data_in(controlled_buffer_1_out), .wr_en(sram_wr), .clk(sram_clk), .cs(dec_4x16_1_dec_out[5]),
    .rd_en(sram_rd), .memory_content(out_13), .data_out(controlled_buffer_1_out));
  sram_cell sram_cell_7 (
    .data_in(controlled_buffer_1_out), .wr_en(sram_wr), .clk(sram_clk), .cs(dec_4x16_1_dec_out[6]),
    .rd_en(sram_rd), .memory_content(out_14), .data_out(controlled_buffer_1_out));
  sram_cell sram_cell_8 (
    .data_in(controlled_buffer_1_out), .wr_en(sram_wr), .clk(sram_clk), .cs(dec_4x16_1_dec_out[7]),
    .rd_en(sram_rd), .memory_content(out_15), .data_out(controlled_buffer_1_out));
  sram_cell sram_cell_9 (
    .data_in(controlled_buffer_1_out), .wr_en(sram_wr), .clk(sram_clk), .cs(dec_4x16_1_dec_out[8]),
    .rd_en(sram_rd), .memory_content(out_16), .data_out(controlled_buffer_1_out));
  sram_cell sram_cell_10 (
    .data_in(controlled_buffer_1_out), .wr_en(sram_wr), .clk(sram_clk), .cs(dec_4x16_1_dec_out[9]),
    .rd_en(sram_rd), .memory_content(out_17), .data_out(controlled_buffer_1_out));
  sram_cell sram_cell_11 (
    .data_in(controlled_buffer_1_out), .wr_en(sram_wr), .clk(sram_clk), .cs(dec_4x16_1_dec_out[10]),
    .rd_en(sram_rd), .memory_content(out_18), .data_out(controlled_buffer_1_out));
  sram_cell sram_cell_12 (
    .data_in(controlled_buffer_1_out), .wr_en(sram_wr), .clk(sram_clk), .cs(dec_4x16_1_dec_out[11]),
    .rd_en(sram_rd), .memory_content(out_19), .data_out(controlled_buffer_1_out));
  sram_cell sram_cell_13 (
    .data_in(controlled_buffer_1_out), .wr_en(sram_wr), .clk(sram_clk), .cs(dec_4x16_1_dec_out[12]),
    .rd_en(sram_rd), .memory_content(out_20), .data_out(controlled_buffer_1_out));
  sram_cell sram_cell_14 (
    .data_in(controlled_buffer_1_out), .wr_en(sram_wr), .clk(sram_clk), .cs(dec_4x16_1_dec_out[13]),
    .rd_en(sram_rd), .memory_content(out_21), .data_out(controlled_buffer_1_out));
  sram_cell sram_cell_15 (
    .data_in(controlled_buffer_1_out), .wr_en(sram_wr), .clk(sram_clk), .cs(dec_4x16_1_dec_out[14]),
    .rd_en(sram_rd), .memory_content(out_22), .data_out(controlled_buffer_1_out));
  sram_cell sram_cell_16 (
    .data_in(controlled_buffer_1_out), .wr_en(sram_wr), .clk(sram_clk), .cs(dec_4x16_1_dec_out[15]),
    .rd_en(sram_rd), .memory_content(out_23), .data_out(controlled_buffer_1_out));
  assign sram_d_out = sram_rd ? controlled_buffer_1_out : 8'bz;  // Controlled_Buffer controlled_buffer_2
endmodule

module ins_reg (
  input  [7:0] ins_reg_in,
  input  ins_reg_in_en,
  input  clk,
  input  ins_reg_out_en,
  output [3:0] add_outs,
  output [3:0] ins_out
);

  wire [3:0] reg_gp_1_reg_int_out;

  reg_gp reg_gp_1 (
    .reg_in(ins_reg_in), .reg_in_en(ins_reg_in_en), .reg_clk(clk),
    .reg_int_out({ins_out, reg_gp_1_reg_int_out}));  // open: reg_out_en, reg_out
  assign add_outs = ins_reg_out_en ? reg_gp_1_reg_int_out : 4'bz;  // Controlled_Buffer controlled_buffer_1
endmodule

module rc (
  input  clk,
  input  ring_reset,
  output T1,
  output T2,
  output T3,
  output T4,
  output T5,
  output T6,
  output T7
);

  wire controlled_buffer_1_out, not_1_out, pull_resistor_1_node;
  wire [3:0] pc_1_pc_value;
  wire [15:7] dec_4x16_1_dec_out;

  Pull_Resistor #(.pull(1)) pull_resistor_1 (.node(pull_resistor_1_node));
  assign controlled_buffer_1_out = ring_reset ? ring_reset : 1'bz;  // Controlled_Buffer controlled_buffer_1
  not not_1 (not_1_out, ring_reset);
  assign controlled_buffer_1_out = not_1_out ? dec_4x16_1_dec_out[7] : 1'bz;  // Controlled_Buffer controlled_buffer_2
  pc pc_1 (
    .pc_en(pull_resistor_1_node), .pc_clk(clk), .pc_reset(controlled_buffer_1_out),
    .pc_out_en(pull_resistor_1_node), .pc_value(pc_1_pc_value));  // open: pc_out
  dec_4x16 dec_4x16_1 (.dec_in(pc_1_pc_value), .dec_out({dec_4x16_1_dec_out, T7, T6, T5, T4, T3, T2, T1}));
endmodule

module cs (
  input  clk,
  input  ring_reset,
  input  [3:0] opcode_in,
  input  debug,
  output ins_in_en,
  output b_in,
  output b_out,
  output sram_wr,
  output a_in,
  output alu_out,
  output alu_sub,
  output shift_in_en,
  output shift_out_en,
  output rotate_in_en,
  output rotate_out_en,
  output a_out,
  output pc_in_en,
  output ins_out_en,
  output sr_amount_in,
  output pc_out_en,
  output ram_rd,
  output pc_en,
  output mar_in,
  output sram_rd
);

  wire and_1_out, and_2_out, and_3_out, and_4_out, and_5_out, and_6_out, and_7_out, and_8_out, and_9_out,
       and_10_out, and_11_out, and_12_out, and_13_out, and_14_out, and_15_out, and_16_out, and_17_out,
       and_18_out, and_19_out, and_21_out, and_22_out, and_23_out, and_24_out, and_25_out, and_26_out,
       and_27_out, and_28_out, and_29_out, and_30_out, and_31_out, and_32_out, and_33_out, and_34_out,
       and_35_out, and_36_out, and_37_out, and_38_out, and_39_out, and_42_out, and_43_out, and_44_out,
       controlled_buffer_1_out, demultiplexer_1_out0, not_1_out, not_2_out, not_3_out, rc_1_t2, rc_1_t3,
       rc_1_t4, rc_1_t5, rc_1_t6, rc_1_t7, ring_reset_t, sram_wr_tunnel;
  wire [3:0] multiplexer_1_out, pull_resistor_1_node;
  wire [15:0] dec_4x16_1_dec_out;

  assign controlled_buffer_1_out = not_1_out ? ring_reset_t : 1'bz;  // Controlled_Buffer controlled_buffer_1
  not not_1 (not_1_out, ring_reset);
  assign controlled_buffer_1_out = ring_reset ? ring_reset : 1'bz;  // Controlled_Buffer controlled_buffer_2
  Pull_Resistor pull_resistor_1 (.node(pull_resistor_1_node));
  Multiplexer #(.width(4)) multiplexer_1 (
    .in0(pull_resistor_1_node), .in1(opcode_in), .out(multiplexer_1_out), .sel(not_2_out));
  not not_2 (not_2_out, debug);
  Pull_Resistor pull_resistor_2 (.node(b_out));
  rc rc_1 (
    .clk(clk), .ring_reset(controlled_buffer_1_out), .T1(pc_out_en), .T2(rc_1_t2), .T3(rc_1_t3),
    .T4(rc_1_t4), .T5(rc_1_t5), .T6(rc_1_t6), .T7(rc_1_t7));
  dec_4x16 dec_4x16_1 (.dec_in(multiplexer_1_out), .dec_out(dec_4x16_1_dec_out));
  and and_1 (and_1_out, rc_1_t3, dec_4x16_1_dec_out[1]);
  or or_1 (mar_in, pc_out_en, and_1_out, and_2_out, and_3_out, and_4_out, and_5_out);
  and and_2 (and_2_out, rc_1_t3, dec_4x16_1_dec_out[2]);
  and and_3 (and_3_out, rc_1_t3, dec_4x16_1_dec_out[3]);
  and and_4 (and_4_out, dec_4x16_1_dec_out[4], rc_1_t3);
  and and_5 (and_5_out, rc_1_t3, dec_4x16_1_dec_out[7]);
  Demultiplexer demultiplexer_1 (.out0(demultiplexer_1_out0), .out1(ram_rd), .in(rc_1_t2), .sel(debug));
  or or_2 (sram_rd, demultiplexer_1_out0, and_6_out, and_7_out);
  and and_6 (and_6_out, rc_1_t4, dec_4x16_1_dec_out[1]);
  and and_7 (and_7_out, rc_1_t4, dec_4x16_1_dec_out[2]);
  Demultiplexer demultiplexer_2 (.out0(ins_in_en), .out1(sram_wr_tunnel), .in(rc_1_t2), .sel(debug));
  not not_3 (not_3_out, dec_4x16_1_dec_out[5]);
  and and_8 (and_8_out, rc_1_t3, not_3_out);
  Demultiplexer demultiplexer_3 (.out0(pc_en), .out1(pc_in_en), .in(and_8_out), .sel(dec_4x16_1_dec_out[9]));
  and and_9 (and_9_out, rc_1_t3, dec_4x16_1_dec_out[1]);
  or or_3 (ins_out_en, and_9_out, and_10_out, and_11_out, and_12_out, and_13_out, and_14_out, and_15_out, and_16_out);
  and and_10 (and_10_out, rc_1_t3, dec_4x16_1_dec_out[2]);
  and and_11 (and_11_out, rc_1_t3, dec_4x16_1_dec_out[3]);
  and and_12 (and_12_out, rc_1_t3, dec_4x16_1_dec_out[4]);
  and and_13 (and_13_out, rc_1_t3, dec_4x16_1_dec_out[6]);
  and and_14 (and_14_out, rc_1_t3, dec_4x16_1_dec_out[7]);
  and and_15 (and_15_out, rc_1_t3, dec_4x16_1_dec_out[8]);
  and and_16 (and_16_out, rc_1_t3, dec_4x16_1_dec_out[9]);
  and and_17 (and_17_out, rc_1_t4, dec_4x16_1_dec_out[1]);
  or or_4 (a_in, and_17_out, and_18_out, and_19_out);
  and and_18 (and_18_out, rc_1_t5, dec_4x16_1_dec_out[6]);
  and and_19 (and_19_out, rc_1_t5, dec_4x16_1_dec_out[8]);
  and and_20 (b_in, dec_4x16_1_dec_out[2], rc_1_t4);
  and and_21 (and_21_out, rc_1_t4, dec_4x16_1_dec_out[0]);
  and and_22 (and_22_out, rc_1_t5, dec_4x16_1_dec_out[1]);
  or or_5 (ring_reset_t, and_21_out, and_22_out, and_23_out, and_24_out, and_25_out, and_26_out, and_27_out, and_28_out, and_29_out, and_30_out);
  and and_23 (and_23_out, dec_4x16_1_dec_out[2], rc_1_t5);
  and and_24 (and_24_out, dec_4x16_1_dec_out[3], rc_1_t5);
  and and_25 (and_25_out, dec_4x16_1_dec_out[5], rc_1_t3);
  and and_26 (and_26_out, dec_4x16_1_dec_out[4], rc_1_t5);
  and and_27 (and_27_out, dec_4x16_1_dec_out[6], rc_1_t6);
  and and_28 (and_28_out, dec_4x16_1_dec_out[7], rc_1_t5);
  and and_29 (and_29_out, dec_4x16_1_dec_out[8], rc_1_t6);
  and and_30 (and_30_out, dec_4x16_1_dec_out[9], rc_1_t4);
  and and_31 (and_31_out, rc_1_t4, dec_4x16_1_dec_out[3]);
  or or_6 (sram_wr, sram_wr_tunnel, and_31_out, and_32_out, and_33_out, and_34_out);
  and and_32 (and_32_out, rc_1_t4, dec_4x16_1_dec_out[4]);
  and and_33 (and_33_out, dec_4x16_1_dec_out[6], rc_1_t7);
  and and_34 (and_34_out, dec_4x16_1_dec_out[7], rc_1_t4);
  and and_35 (and_35_out, rc_1_t4, dec_4x16_1_dec_out[3]);
  and and_36 (and_36_out, rc_1_t4, dec_4x16_1_dec_out[4]);
  or or_7 (alu_out, and_35_out, and_36_out);
  and and_37 (and_37_out, rc_1_t4, dec_4x16_1_dec_out[4]);
  buf or_8 (alu_sub, and_37_out);  // OR_Gate
  and and_38 (and_38_out, dec_4x16_1_dec_out[6], rc_1_t3);
  or or_9 (sr_amount_in, and_38_out, and_39_out);
  and and_39 (and_39_out, dec_4x16_1_dec_out[8], rc_1_t3);
  and and_40 (shift_in_en, dec_4x16_1_dec_out[6], rc_1_t4);
  and and_41 (shift_out_en, dec_4x16_1_dec_out[6], rc_1_t5);
  and and_42 (and_42_out, dec_4x16_1_dec_out[6], rc_1_t4);
  and and_43 (and_43_out, dec_4x16_1_dec_out[7], rc_1_t4);
  or or_10 (a_out, and_42_out, and_43_out, and_44_out);
  and and_44 (and_44_out, dec_4x16_1_dec_out[8], rc_1_t4);
  and and_45 (rotate_in_en, rc_1_t4, dec_4x16_1_dec_out[8]);
  and and_46 (rotate_out_en, rc_1_t5, dec_4x16_1_dec_out[8]);

  // Other names for the same wires on the sheet: a_out_t = b_out; alu_out_t = b_out; alu_sub_t = b_out

  // Notes on the sheet:
  //   0. Debug
  //   1. LDA
  //   2.LDB
  //   3. OUT
  //   4. SUB
  //   5. HLT
  //   6. SHT
  //   7. STA
  //   8. RTE
  //   9. JMP
endmodule

module b_shifter (
  input  [7:0] data,
  input  shift_out_en,
  input  shift_in_en,
  input  clk,
  input  [7:0] d_n_amount,
  input  shift_amount_in,
  output [7:0] shift_data_out
);

  wire multiplexer_2_out, multiplexer_3_out, multiplexer_4_out, multiplexer_5_out, multiplexer_6_out,
       multiplexer_7_out, multiplexer_8_out, multiplexer_9_out, multiplexer_10_out, multiplexer_11_out,
       multiplexer_12_out, multiplexer_13_out, multiplexer_14_out, multiplexer_15_out, multiplexer_16_out,
       multiplexer_17_out, pull_resistor_1_node;
  wire [7:0] multiplexer_1_out, multiplexer_18_out, multiplexer_26_out, reg_gp_1_reg_int_out,
       reg_gp_2_reg_int_out, reg_gp_3_reg_int_out;

  reg_gp reg_gp_1 (
    .reg_in(data), .reg_in_en(shift_in_en), .reg_clk(clk), .reg_int_out(reg_gp_1_reg_int_out));  // open: reg_out_en, reg_out
  Multiplexer #(.width(8)) multiplexer_1 (
    .in0({reg_gp_1_reg_int_out[0], reg_gp_1_reg_int_out[1], reg_gp_1_reg_int_out[2], reg_gp_1_reg_int_out[3], reg_gp_1_reg_int_out[4], reg_gp_1_reg_int_out[5], reg_gp_1_reg_int_out[6], reg_gp_1_reg_int_out[7]}),
    .in1(reg_gp_1_reg_int_out), .out(multiplexer_1_out), .sel(reg_gp_2_reg_int_out[3]));
  reg_gp reg_gp_2 (
    .reg_in(d_n_amount), .reg_in_en(shift_amount_in), .reg_clk(clk), .reg_int_out(reg_gp_2_reg_int_out));  // open: reg_out_en, reg_out
  Multiplexer multiplexer_2 (
    .in0(multiplexer_1_out[7]), .in1(multiplexer_1_out[6]), .out(multiplexer_2_out),
    .sel(reg_gp_2_reg_int_out[0]));
  Multiplexer multiplexer_3 (
    .in0(multiplexer_1_out[6]), .in1(multiplexer_1_out[5]), .out(multiplexer_3_out),
    .sel(reg_gp_2_reg_int_out[0]));
  Multiplexer multiplexer_4 (
    .in0(multiplexer_1_out[5]), .in1(multiplexer_1_out[4]), .out(multiplexer_4_out),
    .sel(reg_gp_2_reg_int_out[0]));
  Multiplexer multiplexer_5 (
    .in0(multiplexer_1_out[4]), .in1(multiplexer_1_out[3]), .out(multiplexer_5_out),
    .sel(reg_gp_2_reg_int_out[0]));
  Multiplexer multiplexer_6 (
    .in0(multiplexer_1_out[3]), .in1(multiplexer_1_out[2]), .out(multiplexer_6_out),
    .sel(reg_gp_2_reg_int_out[0]));
  Multiplexer multiplexer_7 (
    .in0(multiplexer_1_out[2]), .in1(multiplexer_1_out[1]), .out(multiplexer_7_out),
    .sel(reg_gp_2_reg_int_out[0]));
  Multiplexer multiplexer_8 (
    .in0(multiplexer_1_out[1]), .in1(multiplexer_1_out[0]), .out(multiplexer_8_out),
    .sel(reg_gp_2_reg_int_out[0]));
  Multiplexer multiplexer_9 (
    .in0(multiplexer_1_out[0]), .in1(1'b0), .out(multiplexer_9_out), .sel(reg_gp_2_reg_int_out[0]));
  Multiplexer multiplexer_10 (
    .in0(multiplexer_2_out), .in1(multiplexer_4_out), .out(multiplexer_10_out), .sel(reg_gp_2_reg_int_out[1]));
  Multiplexer multiplexer_11 (
    .in0(multiplexer_3_out), .in1(multiplexer_5_out), .out(multiplexer_11_out), .sel(reg_gp_2_reg_int_out[1]));
  Multiplexer multiplexer_12 (
    .in0(multiplexer_4_out), .in1(multiplexer_6_out), .out(multiplexer_12_out), .sel(reg_gp_2_reg_int_out[1]));
  Multiplexer multiplexer_13 (
    .in0(multiplexer_5_out), .in1(multiplexer_7_out), .out(multiplexer_13_out), .sel(reg_gp_2_reg_int_out[1]));
  Multiplexer multiplexer_14 (
    .in0(multiplexer_6_out), .in1(multiplexer_8_out), .out(multiplexer_14_out), .sel(reg_gp_2_reg_int_out[1]));
  Multiplexer multiplexer_15 (
    .in0(multiplexer_7_out), .in1(multiplexer_9_out), .out(multiplexer_15_out), .sel(reg_gp_2_reg_int_out[1]));
  Multiplexer multiplexer_16 (
    .in0(multiplexer_8_out), .in1(1'b0), .out(multiplexer_16_out), .sel(reg_gp_2_reg_int_out[1]));
  Multiplexer multiplexer_17 (
    .in0(multiplexer_9_out), .in1(1'b0), .out(multiplexer_17_out), .sel(reg_gp_2_reg_int_out[1]));
  Multiplexer multiplexer_18 (
    .in0(multiplexer_10_out), .in1(multiplexer_14_out), .out(multiplexer_18_out[7]),
    .sel(reg_gp_2_reg_int_out[2]));
  Multiplexer multiplexer_19 (
    .in0(multiplexer_11_out), .in1(multiplexer_15_out), .out(multiplexer_18_out[6]),
    .sel(reg_gp_2_reg_int_out[2]));
  Multiplexer multiplexer_20 (
    .in0(multiplexer_12_out), .in1(multiplexer_16_out), .out(multiplexer_18_out[5]),
    .sel(reg_gp_2_reg_int_out[2]));
  Multiplexer multiplexer_21 (
    .in0(multiplexer_13_out), .in1(multiplexer_17_out), .out(multiplexer_18_out[4]),
    .sel(reg_gp_2_reg_int_out[2]));
  Multiplexer multiplexer_22 (
    .in0(multiplexer_14_out), .in1(1'b0), .out(multiplexer_18_out[3]), .sel(reg_gp_2_reg_int_out[2]));
  Multiplexer multiplexer_23 (
    .in0(multiplexer_15_out), .in1(1'b0), .out(multiplexer_18_out[2]), .sel(reg_gp_2_reg_int_out[2]));
  Multiplexer multiplexer_24 (
    .in0(multiplexer_16_out), .in1(1'b0), .out(multiplexer_18_out[1]), .sel(reg_gp_2_reg_int_out[2]));
  Multiplexer multiplexer_25 (
    .in0(multiplexer_17_out), .in1(1'b0), .out(multiplexer_18_out[0]), .sel(reg_gp_2_reg_int_out[2]));
  Multiplexer #(.width(8)) multiplexer_26 (
    .in0({multiplexer_18_out[0], multiplexer_18_out[1], multiplexer_18_out[2], multiplexer_18_out[3], multiplexer_18_out[4], multiplexer_18_out[5], multiplexer_18_out[6], multiplexer_18_out[7]}),
    .in1(multiplexer_18_out), .out(multiplexer_26_out), .sel(reg_gp_2_reg_int_out[3]));
  Pull_Resistor #(.pull(1)) pull_resistor_1 (.node(pull_resistor_1_node));
  reg_gp reg_gp_3 (
    .reg_in(multiplexer_26_out), .reg_in_en(pull_resistor_1_node), .reg_clk(clk), .reg_out_en(shift_out_en),
    .reg_int_out(reg_gp_3_reg_int_out), .reg_out(shift_data_out));
endmodule

module rotator (
  input  [7:0] data,
  input  rotate_out_en,
  input  rotate_in_en,
  input  clk,
  input  [7:0] d_n_amount,
  input  rotate_amount_in,
  output [7:0] rotate_data_out
);

  wire multiplexer_2_out, multiplexer_3_out, multiplexer_4_out, multiplexer_5_out, multiplexer_6_out,
       multiplexer_7_out, multiplexer_8_out, multiplexer_9_out, multiplexer_10_out, multiplexer_11_out,
       multiplexer_12_out, multiplexer_13_out, multiplexer_14_out, multiplexer_15_out, multiplexer_16_out,
       multiplexer_17_out, pull_resistor_1_node;
  wire [7:0] multiplexer_1_out, multiplexer_18_out, multiplexer_26_out, reg_gp_1_reg_int_out,
       reg_gp_2_reg_int_out, reg_gp_3_reg_int_out;

  reg_gp reg_gp_1 (
    .reg_in(data), .reg_in_en(rotate_in_en), .reg_clk(clk), .reg_int_out(reg_gp_1_reg_int_out));  // open: reg_out_en, reg_out
  Multiplexer #(.width(8)) multiplexer_1 (
    .in0({reg_gp_1_reg_int_out[0], reg_gp_1_reg_int_out[1], reg_gp_1_reg_int_out[2], reg_gp_1_reg_int_out[3], reg_gp_1_reg_int_out[4], reg_gp_1_reg_int_out[5], reg_gp_1_reg_int_out[6], reg_gp_1_reg_int_out[7]}),
    .in1(reg_gp_1_reg_int_out), .out(multiplexer_1_out), .sel(reg_gp_2_reg_int_out[3]));
  reg_gp reg_gp_2 (
    .reg_in(d_n_amount), .reg_in_en(rotate_amount_in), .reg_clk(clk), .reg_int_out(reg_gp_2_reg_int_out));  // open: reg_out_en, reg_out
  Multiplexer multiplexer_2 (
    .in0(multiplexer_1_out[7]), .in1(multiplexer_1_out[6]), .out(multiplexer_2_out),
    .sel(reg_gp_2_reg_int_out[0]));
  Multiplexer multiplexer_3 (
    .in0(multiplexer_1_out[6]), .in1(multiplexer_1_out[5]), .out(multiplexer_3_out),
    .sel(reg_gp_2_reg_int_out[0]));
  Multiplexer multiplexer_4 (
    .in0(multiplexer_1_out[5]), .in1(multiplexer_1_out[4]), .out(multiplexer_4_out),
    .sel(reg_gp_2_reg_int_out[0]));
  Multiplexer multiplexer_5 (
    .in0(multiplexer_1_out[4]), .in1(multiplexer_1_out[3]), .out(multiplexer_5_out),
    .sel(reg_gp_2_reg_int_out[0]));
  Multiplexer multiplexer_6 (
    .in0(multiplexer_1_out[3]), .in1(multiplexer_1_out[2]), .out(multiplexer_6_out),
    .sel(reg_gp_2_reg_int_out[0]));
  Multiplexer multiplexer_7 (
    .in0(multiplexer_1_out[2]), .in1(multiplexer_1_out[1]), .out(multiplexer_7_out),
    .sel(reg_gp_2_reg_int_out[0]));
  Multiplexer multiplexer_8 (
    .in0(multiplexer_1_out[1]), .in1(multiplexer_1_out[0]), .out(multiplexer_8_out),
    .sel(reg_gp_2_reg_int_out[0]));
  Multiplexer multiplexer_9 (
    .in0(multiplexer_1_out[0]), .in1(multiplexer_1_out[7]), .out(multiplexer_9_out),
    .sel(reg_gp_2_reg_int_out[0]));
  Multiplexer multiplexer_10 (
    .in0(multiplexer_2_out), .in1(multiplexer_4_out), .out(multiplexer_10_out), .sel(reg_gp_2_reg_int_out[1]));
  Multiplexer multiplexer_11 (
    .in0(multiplexer_3_out), .in1(multiplexer_5_out), .out(multiplexer_11_out), .sel(reg_gp_2_reg_int_out[1]));
  Multiplexer multiplexer_12 (
    .in0(multiplexer_4_out), .in1(multiplexer_6_out), .out(multiplexer_12_out), .sel(reg_gp_2_reg_int_out[1]));
  Multiplexer multiplexer_13 (
    .in0(multiplexer_5_out), .in1(multiplexer_7_out), .out(multiplexer_13_out), .sel(reg_gp_2_reg_int_out[1]));
  Multiplexer multiplexer_14 (
    .in0(multiplexer_6_out), .in1(multiplexer_8_out), .out(multiplexer_14_out), .sel(reg_gp_2_reg_int_out[1]));
  Multiplexer multiplexer_15 (
    .in0(multiplexer_7_out), .in1(multiplexer_9_out), .out(multiplexer_15_out), .sel(reg_gp_2_reg_int_out[1]));
  Multiplexer multiplexer_16 (
    .in0(multiplexer_8_out), .in1(multiplexer_2_out), .out(multiplexer_16_out), .sel(reg_gp_2_reg_int_out[1]));
  Multiplexer multiplexer_17 (
    .in0(multiplexer_9_out), .in1(multiplexer_3_out), .out(multiplexer_17_out), .sel(reg_gp_2_reg_int_out[1]));
  Multiplexer multiplexer_18 (
    .in0(multiplexer_10_out), .in1(multiplexer_14_out), .out(multiplexer_18_out[7]),
    .sel(reg_gp_2_reg_int_out[2]));
  Multiplexer multiplexer_19 (
    .in0(multiplexer_11_out), .in1(multiplexer_15_out), .out(multiplexer_18_out[6]),
    .sel(reg_gp_2_reg_int_out[2]));
  Multiplexer multiplexer_20 (
    .in0(multiplexer_12_out), .in1(multiplexer_16_out), .out(multiplexer_18_out[5]),
    .sel(reg_gp_2_reg_int_out[2]));
  Multiplexer multiplexer_21 (
    .in0(multiplexer_13_out), .in1(multiplexer_17_out), .out(multiplexer_18_out[4]),
    .sel(reg_gp_2_reg_int_out[2]));
  Multiplexer multiplexer_22 (
    .in0(multiplexer_14_out), .in1(multiplexer_10_out), .out(multiplexer_18_out[3]),
    .sel(reg_gp_2_reg_int_out[2]));
  Multiplexer multiplexer_23 (
    .in0(multiplexer_15_out), .in1(multiplexer_11_out), .out(multiplexer_18_out[2]),
    .sel(reg_gp_2_reg_int_out[2]));
  Multiplexer multiplexer_24 (
    .in0(multiplexer_16_out), .in1(multiplexer_12_out), .out(multiplexer_18_out[1]),
    .sel(reg_gp_2_reg_int_out[2]));
  Multiplexer multiplexer_25 (
    .in0(multiplexer_17_out), .in1(multiplexer_13_out), .out(multiplexer_18_out[0]),
    .sel(reg_gp_2_reg_int_out[2]));
  Pull_Resistor #(.pull(1)) pull_resistor_1 (.node(pull_resistor_1_node));
  Multiplexer #(.width(8)) multiplexer_26 (
    .in0({multiplexer_18_out[0], multiplexer_18_out[1], multiplexer_18_out[2], multiplexer_18_out[3], multiplexer_18_out[4], multiplexer_18_out[5], multiplexer_18_out[6], multiplexer_18_out[7]}),
    .in1(multiplexer_18_out), .out(multiplexer_26_out), .sel(reg_gp_2_reg_int_out[3]));
  reg_gp reg_gp_3 (
    .reg_in(multiplexer_26_out), .reg_in_en(pull_resistor_1_node), .reg_clk(clk), .reg_out_en(rotate_out_en),
    .reg_int_out(reg_gp_3_reg_int_out), .reg_out(rotate_data_out));
endmodule

module pcWithLoader (
  input  pc_en,
  input  [3:0] pc_in,
  input  pc_in_en,
  input  pc_reset,
  input  pc_clk,
  input  pc_out_en,
  output [3:0] pc_value,
  output [3:0] pc_out
);

  wire and_1_out, and_2_out, and_3_out, multiplexer_1_out, multiplexer_2_out, multiplexer_3_out,
       multiplexer_4_out, multiplexer_5_out, multiplexer_6_out, multiplexer_7_out, multiplexer_8_out,
       not_1_out, not_2_out, not_3_out, not_4_out;

  Multiplexer multiplexer_1 (.in0(and_1_out), .in1(not_1_out), .out(multiplexer_1_out), .sel(pc_in_en));
  and and_1 (and_1_out, pc_en, pc_value[2], pc_value[1], pc_value[0]);
  not not_1 (not_1_out, pc_in[3]);
  Multiplexer multiplexer_2 (.in0(and_1_out), .in1(pc_in[3]), .out(multiplexer_2_out), .sel(pc_in_en));
  J_K_Flip_Flop j_k_ff_1 (
    .J(multiplexer_2_out), .K(multiplexer_1_out), .clk(pc_clk), .Q(pc_value[3]), .reset(pc_reset));  // open: Qn, preset
  and and_2 (and_2_out, pc_en, pc_value[1], pc_value[0]);
  Multiplexer multiplexer_3 (.in0(and_2_out), .in1(pc_in[2]), .out(multiplexer_3_out), .sel(pc_in_en));
  Multiplexer multiplexer_4 (.in0(and_2_out), .in1(not_2_out), .out(multiplexer_4_out), .sel(pc_in_en));
  J_K_Flip_Flop j_k_ff_2 (
    .J(multiplexer_3_out), .K(multiplexer_4_out), .clk(pc_clk), .Q(pc_value[2]), .reset(pc_reset));  // open: Qn, preset
  not not_2 (not_2_out, pc_in[2]);
  and and_3 (and_3_out, pc_en, pc_value[0]);
  Multiplexer multiplexer_5 (.in0(and_3_out), .in1(pc_in[1]), .out(multiplexer_5_out), .sel(pc_in_en));
  not not_3 (not_3_out, pc_in[1]);
  Multiplexer multiplexer_6 (.in0(and_3_out), .in1(not_3_out), .out(multiplexer_6_out), .sel(pc_in_en));
  J_K_Flip_Flop j_k_ff_3 (
    .J(multiplexer_5_out), .K(multiplexer_6_out), .clk(pc_clk), .Q(pc_value[1]), .reset(pc_reset));  // open: Qn, preset
  J_K_Flip_Flop j_k_ff_4 (
    .J(multiplexer_7_out), .K(multiplexer_8_out), .clk(pc_clk), .Q(pc_value[0]), .reset(pc_reset));  // open: Qn, preset
  not not_4 (not_4_out, pc_in[0]);
  Multiplexer multiplexer_7 (.in0(pc_en), .in1(pc_in[0]), .out(multiplexer_7_out), .sel(pc_in_en));
  Multiplexer multiplexer_8 (.in0(pc_en), .in1(not_4_out), .out(multiplexer_8_out), .sel(pc_in_en));
  assign pc_out = pc_out_en ? pc_value : 4'bz;  // Controlled_Buffer controlled_buffer_1
endmodule
